// Logisim project single_cycle_processor.circ as structural Verilog: 12 circuits, main circuit main
module main (
  input  in_1,
  input  in_2,
  output [4:0] Read_Register_1,
  output [31:0] out_4,
  output [31:0] out_5,
  output [31:0] out_6,
  output [31:0] out_7,
  output [31:0] out_8,
  output [31:0] out_9,
  output [31:0] out_10
);

  wire alu_1_zero, and_1_out, clock_1_out, control_unit_1_alusrc, control_unit_1_branch,
       control_unit_1_memread, control_unit_1_memtoreg, control_unit_1_memwrite, control_unit_1_regwrite;
  wire [2:0] instr_decoder_1_funct3;
  wire [3:0] control_unit_1_aluop;
  wire [4:0] instr_decoder_1_inst_11_to_7, instr_decoder_1_inst_20_to_24;
  wire [6:0] instr_decoder_1_funct7, instr_decoder_1_inst_6_to_0;
  wire [23:0] adder_1_out, adder_2_out, bit_extender_1_out, bit_extender_2_out, n2x1_mux_24_bit_1_out_4,
       register_1_q;
  wire [31:0] instr_decoder_1_inst_31_to_0, ram_1_data, shifter_1_out;

  Clock clock_1 (.out(clock_1_out));
  Register #(.width(24)) register_1 (
    .D(n2x1_mux_24_bit_1_out_4), .Q(register_1_q), .clk(clock_1_out), .clr(in_2));  // open: en
  ROM #(.addrWidth(24), .dataWidth(32)) rom_1 (.addr(register_1_q), .data(out_10));  // open: sel
  instr_decoder instr_decoder_1 (
    .in_1(out_10), .inst_6_to_0(instr_decoder_1_inst_6_to_0), .funct3(instr_decoder_1_funct3),
    .inst_19_to_15(Read_Register_1), .inst_20_to_24(instr_decoder_1_inst_20_to_24),
    .inst_11_to_7(instr_decoder_1_inst_11_to_7), .inst_31_to_0(instr_decoder_1_inst_31_to_0),
    .funct7(instr_decoder_1_funct7));
  control_unit control_unit_1 (
    .opcode(instr_decoder_1_inst_6_to_0), .funct3(instr_decoder_1_funct3), .funct7(instr_decoder_1_funct7),
    .Branch(control_unit_1_branch), .MemRead(control_unit_1_memread), .MemtoReg(control_unit_1_memtoreg),
    .MemWrite(control_unit_1_memwrite), .ALUSrc(control_unit_1_alusrc), .RegWrite(control_unit_1_regwrite),
    .ALUOp(control_unit_1_aluop));
  imm_Gen imm_gen_1 (.in_1(instr_decoder_1_inst_31_to_0), .out_2(out_6));
  Register_File register_file_1 (
    .rs1(Read_Register_1), .rs2(instr_decoder_1_inst_20_to_24), .rd(instr_decoder_1_inst_11_to_7),
    .Write_Data(out_5), .RegWEn(control_unit_1_regwrite), .Clock(clock_1_out), .Read_Data_1(out_4),
    .Read_Data_2(out_9), .in_7(in_1));
  _2X1_mux u_2x1_mux_1 (.in_1(out_9), .in_2(out_6), .in_3(control_unit_1_alusrc), .out_4(out_7));
  Shifter #(.width(32)) shifter_1 (.in(out_6), .\dist (5'b00001), .out(shifter_1_out));
  Bit_Extender #(.in_width(32), .out_width(24)) bit_extender_1 (.in(shifter_1_out), .out(bit_extender_1_out));
  ALU alu_1 (.A(out_4), .B(out_7), .ALUSel(control_unit_1_aluop), .Result(out_8), .Zero(alu_1_zero));  // open: OverFlow
  Bit_Extender #(.in_width(32), .out_width(24)) bit_extender_2 (.in(out_8), .out(bit_extender_2_out));
  Adder #(.width(24)) adder_1 (.a(register_1_q), .b(24'h4), .out(adder_1_out));  // open: cin, cout
  Adder #(.width(24)) adder_2 (.a(register_1_q), .b(bit_extender_1_out), .out(adder_2_out));  // open: cin, cout
  and and_1 (and_1_out, control_unit_1_branch, alu_1_zero);
  _2X1_mux_24_bit u_2x1_mux_24_bit_1 (
    .in_1(adder_1_out), .in_2(adder_2_out), .in_3(and_1_out), .out_4(n2x1_mux_24_bit_1_out_4));
  RAM #(.addrWidth(24), .dataWidth(32), .bus("separate")) ram_1 (
    .addr(bit_extender_2_out), .din(out_9), .data(ram_1_data), .str(control_unit_1_memwrite),
    .clk(clock_1_out), .ld(control_unit_1_memread));  // open: sel, clr
  _2X1_mux u_2x1_mux_2 (.in_1(out_8), .in_2(ram_1_data), .in_3(control_unit_1_memtoreg), .out_4(out_5));

  // Notes on the sheet:
  //   SATWIK 2022CS51150
  //           ABHIJEET CHOUDHARY 2022CS11104
  //   Instruction
  //   Read_data1
  //        Write Data
  //   Immediate
  //   ALU_input
  //   ALU OUT
  //   Read_data2
endmodule

module instr_decoder (
  input  [31:0] in_1,
  output [6:0] inst_6_to_0,
  output [2:0] funct3,
  output [4:0] inst_19_to_15,
  output [4:0] inst_20_to_24,
  output [4:0] inst_11_to_7,
  output [31:0] inst_31_to_0,
  output [6:0] funct7
);


  assign funct3 = in_1[14:12];
  assign funct7 = in_1[31:25];
  assign inst_6_to_0 = in_1[6:0];
  assign inst_11_to_7 = in_1[11:7];
  assign inst_19_to_15 = in_1[19:15];
  assign inst_20_to_24 = in_1[24:20];
  assign inst_31_to_0 = in_1;
endmodule

module control_unit (
  input  [6:0] opcode,
  input  [6:0] funct7,
  input  [2:0] funct3,
  output Branch,
  output MemRead,
  output MemtoReg,
  output [3:0] ALUOp,
  output MemWrite,
  output ALUSrc,
  output RegWrite
);

  wire and_1_out, comparator_1_eq, comparator_2_eq, comparator_4_eq, comparator_5_eq, or_1_out;
  wire [3:0] and_2_out, and_3_out, bit_extender_1_out, bit_extender_2_out, bit_extender_3_out,
       bit_extender_4_out, multiplier_1_out, or_4_out;

  assign bit_extender_1_out = {{1{1'b0}}, funct3};  // Bit_Extender bit_extender_1
  Comparator #(.width(3), .mode("unsigned")) comparator_1 (
    .a(funct3), .b(3'b000), .eq(comparator_1_eq));  // open: gt, lt
  Comparator #(.width(7), .mode("unsigned")) comparator_2 (
    .a(funct7), .b(7'b0100000), .eq(comparator_2_eq));  // open: gt, lt
  Comparator #(.width(7)) comparator_3 (.a(opcode), .b(7'b0000011), .eq(MemRead));  // open: gt, lt
  Comparator #(.width(7)) comparator_4 (.a(opcode), .b(7'b0010011), .eq(comparator_4_eq));  // open: gt, lt
  Comparator #(.width(7)) comparator_5 (.a(opcode), .b(7'b0110011), .eq(comparator_5_eq));  // open: gt, lt
  Comparator #(.width(7)) comparator_6 (.a(opcode), .b(7'b0100011), .eq(MemWrite));  // open: gt, lt
  Comparator #(.width(7)) comparator_7 (.a(opcode), .b(7'b1100011), .eq(Branch));  // open: gt, lt
  and and_1 (and_1_out, comparator_1_eq, comparator_2_eq);
  or or_1 (or_1_out, comparator_5_eq, comparator_4_eq);
  assign bit_extender_2_out = {{3{1'b0}}, and_1_out};  // Bit_Extender bit_extender_2
  or or_2 (RegWrite, MemRead, comparator_4_eq, comparator_5_eq);
  Multiplier #(.width(4)) multiplier_1 (
    .a(bit_extender_2_out), .b(4'b1100), .out(multiplier_1_out));  // open: cin, cout
  or or_3 (ALUSrc, MemRead, comparator_4_eq, MemWrite);
  assign bit_extender_3_out = {{3{or_1_out}}, or_1_out};  // Bit_Extender bit_extender_3
  assign or_4_out = multiplier_1_out | bit_extender_1_out;  // OR_Gate or_4, 4 bits wide
  assign and_2_out = bit_extender_3_out & or_4_out;  // AND_Gate and_2, 4 bits wide
  assign bit_extender_4_out = {{3{Branch}}, Branch};  // Bit_Extender bit_extender_4
  assign and_3_out = bit_extender_4_out & 4'b1100;  // AND_Gate and_3, 4 bits wide
  assign ALUOp = and_2_out | and_3_out;  // OR_Gate or_5, 4 bits wide

  assign MemtoReg = MemRead;

  // Notes on the sheet:
  //   lw
  //   imm
  //   r type
  //   sw
  //   beq
endmodule

module ALU (
  input  [31:0] A,
  input  [31:0] B,
  input  [3:0] ALUSel,
  output OverFlow,
  output [31:0] Result,
  output Zero
);

  wire adder_1_cout, comparator_1_lt, comparator_2_lt, not_1_out, not_2_out, not_3_out, not_4_out, or_2_out,
       or_3_out, xor_2_out;
  wire [31:0] adder_1_out, and_1_out, bit_extender_1_out, bit_extender_2_out, multiplier_1_cout,
       multiplier_1_out, or_1_out, shifter_1_out, shifter_2_out, shifter_3_out, subtractor_1_out, undriven,
       xor_1_out;

  Adder #(.width(32)) adder_1 (.a(A), .b(B), .out(adder_1_out), .cin(1'b0), .cout(adder_1_cout));
  Shifter #(.width(32)) shifter_1 (.in(A), .\dist (B[4:0]), .out(shifter_1_out));
  Comparator #(.width(32)) comparator_1 (.a(A), .b(B), .lt(comparator_1_lt));  // open: gt, eq
  assign xor_1_out = A ^ B;  // XOR_Gate xor_1, 32 bits wide
  Shifter #(.width(32), .shift("lr")) shifter_2 (.in(A), .\dist (B[4:0]), .out(shifter_2_out));
  assign or_1_out = A | B;  // OR_Gate or_1, 32 bits wide
  assign and_1_out = A & B;  // AND_Gate and_1, 32 bits wide
  Multiplier #(.width(32)) multiplier_1 (
    .a(A), .b(B), .out(multiplier_1_out), .cin({32{1'b0}}), .cout(multiplier_1_cout));
  Subtractor #(.width(32)) subtractor_1 (.a(A), .b(B), .out(subtractor_1_out), .bin(1'b0));  // open: bout
  Shifter #(.width(32), .shift("ar")) shifter_3 (.in(A), .\dist (B[4:0]), .out(shifter_3_out));
  Comparator #(.width(32), .mode("unsigned")) comparator_2 (.a(A), .b(B), .lt(comparator_2_lt));  // open: gt, eq
  assign bit_extender_1_out = {{31{1'b0}}, comparator_1_lt};  // Bit_Extender bit_extender_1
  assign bit_extender_2_out = {{31{1'b0}}, comparator_2_lt};  // Bit_Extender bit_extender_2
  not not_1 (not_1_out, xor_2_out);
  xor xor_2 (xor_2_out, A[31], B[31]);
  _16X1_mux u_16x1_mux_1 (
    .in0(adder_1_out), .in1(shifter_1_out), .in2(bit_extender_1_out), .in3(bit_extender_2_out),
    .in4(xor_1_out), .in5(shifter_2_out), .in6(or_1_out), .sel3(ALUSel[3]), .sel2(ALUSel[2]),
    .sel1(ALUSel[1]), .in7(and_1_out), .sel0(ALUSel[0]), .in8(multiplier_1_out), .in9(multiplier_1_cout),
    .in11(undriven), .in12(subtractor_1_out), .in13(shifter_3_out), .in15(B), .\output (Result));  // open: in10, in14
  and and_2 (OverFlow, adder_1_cout, not_1_out, not_2_out);
  not not_2 (not_2_out, or_2_out);
  or or_2 (or_2_out, ALUSel[0], ALUSel[1], ALUSel[2], ALUSel[3]);
  not not_3 (not_3_out, OverFlow);
  or or_3 (or_3_out, Result[0], Result[1], Result[2], Result[3], Result[4], Result[5], Result[6], Result[7], Result[8], Result[9], Result[10], Result[11], Result[12], Result[13], Result[14], Result[15], Result[17], Result[18], Result[19], Result[20], Result[21], Result[22], Result[23], Result[24], Result[25], Result[26], Result[27], Result[28], Result[29], Result[30], Result[31], Result[16]);
  not not_4 (not_4_out, or_3_out);
  and and_3 (Zero, not_3_out, not_4_out);

  // Notes on the sheet:
  //   Abhijeet Choudhary 2022CS11104 , Satwik 2022CS51150
endmodule

module _2X1_mux (
  input  [31:0] in_1,
  input  [31:0] in_2,
  input  in_3,
  output [31:0] out_4
);

  wire [31:0] and_1_out, and_2_out, bit_extender_1_out, not_1_out;

  assign bit_extender_1_out = {{31{in_3}}, in_3};  // Bit_Extender bit_extender_1
  assign not_1_out = ~bit_extender_1_out;  // NOT_Gate not_1, 32 bits wide
  assign and_1_out = in_1 & not_1_out;  // AND_Gate and_1, 32 bits wide
  assign and_2_out = in_2 & bit_extender_1_out;  // AND_Gate and_2, 32 bits wide
  assign out_4 = and_1_out | and_2_out;  // OR_Gate or_1, 32 bits wide
endmodule

module _4X1_mux (
  input  [31:0] in0,
  input  [31:0] in1,
  input  [31:0] in2,
  input  [31:0] in3,
  input  sel0,
  input  sel1,
  output [31:0] out
);

  wire [31:0] n2x1_mux_1_out_4, n2x1_mux_2_out_4;

  _2X1_mux u_2x1_mux_1 (.in_1(in0), .in_2(in1), .in_3(sel1), .out_4(n2x1_mux_1_out_4));
  _2X1_mux u_2x1_mux_2 (.in_1(in2), .in_2(in3), .in_3(sel1), .out_4(n2x1_mux_2_out_4));
  _2X1_mux u_2x1_mux_3 (.in_1(n2x1_mux_1_out_4), .in_2(n2x1_mux_2_out_4), .in_3(sel0), .out_4(out));
endmodule

module _16X1_mux (
  input  [31:0] in0,
  input  [31:0] in1,
  input  [31:0] in2,
  input  [31:0] in3,
  input  [31:0] in4,
  input  [31:0] in5,
  input  [31:0] in6,
  input  sel3,
  input  sel2,
  input  sel1,
  input  [31:0] in7,
  input  sel0,
  input  [31:0] in8,
  input  [31:0] in9,
  input  [31:0] in10,
  input  [31:0] in11,
  input  [31:0] in12,
  input  [31:0] in13,
  input  [31:0] in14,
  input  [31:0] in15,
  output [31:0] \output 
);

  wire [31:0] n4x1_mux_1_out, n4x1_mux_2_out, n4x1_mux_3_out, n4x1_mux_4_out;

  _4X1_mux u_4x1_mux_1 (.in0(in0), .in1(in1), .in2(in2), .in3(in3), .sel0(sel1), .sel1(sel0), .out(n4x1_mux_1_out));
  _4X1_mux u_4x1_mux_2 (.in0(in4), .in1(in5), .in2(in6), .in3(in7), .sel0(sel1), .sel1(sel0), .out(n4x1_mux_2_out));
  _4X1_mux u_4x1_mux_3 (.in0(in8), .in1(in9), .in2(in10), .in3(in11), .sel0(sel1), .sel1(sel0), .out(n4x1_mux_3_out));
  _4X1_mux u_4x1_mux_4 (.in0(in12), .in1(in13), .in2(in14), .in3(in15), .sel0(sel1), .sel1(sel0), .out(n4x1_mux_4_out));
  _4X1_mux u_4x1_mux_5 (
    .in0(n4x1_mux_1_out), .in1(n4x1_mux_2_out), .in2(n4x1_mux_3_out), .in3(n4x1_mux_4_out), .sel0(sel3),
    .sel1(sel2), .out(\output ));
endmodule

module imm_Gen (
  input  [31:0] in_1,
  output [31:0] out_2
);

  wire comparator_1_eq, comparator_2_eq, comparator_3_eq, comparator_4_eq;
  wire [31:0] and_1_out, and_2_out, and_3_out, and_4_out, bit_extender_1_out, bit_extender_2_out,
       bit_extender_3_out, bit_extender_4_out, bit_extender_5_out, bit_extender_6_out, bit_extender_7_out;

  assign bit_extender_1_out = {{31{comparator_1_eq}}, comparator_1_eq};  // Bit_Extender bit_extender_1
  Comparator #(.width(7)) comparator_1 (.a(in_1[6:0]), .b(7'b0000011), .eq(comparator_1_eq));  // open: gt, lt
  assign bit_extender_2_out = {{31{comparator_2_eq}}, comparator_2_eq};  // Bit_Extender bit_extender_2
  Comparator #(.width(7)) comparator_2 (.a(in_1[6:0]), .b(7'b0010011), .eq(comparator_2_eq));  // open: gt, lt
  assign bit_extender_3_out = {{31{comparator_3_eq}}, comparator_3_eq};  // Bit_Extender bit_extender_3
  Comparator #(.width(7)) comparator_3 (.a(in_1[6:0]), .b(7'b0100011), .eq(comparator_3_eq));  // open: gt, lt
  Comparator #(.width(7)) comparator_4 (.a(in_1[6:0]), .b(7'b1100011), .eq(comparator_4_eq));  // open: gt, lt
  assign bit_extender_4_out = {{31{comparator_4_eq}}, comparator_4_eq};  // Bit_Extender bit_extender_4
  assign bit_extender_5_out = {{20{in_1[31]}}, in_1[31:20]};  // Bit_Extender bit_extender_5
  assign bit_extender_6_out = {{20{in_1[31]}}, {in_1[31:25], in_1[11:7]}};  // Bit_Extender bit_extender_6
  assign bit_extender_7_out = {{20{in_1[31]}}, {in_1[31], in_1[7], in_1[30:25], in_1[11:8]}};  // Bit_Extender bit_extender_7
  assign and_1_out = bit_extender_1_out & bit_extender_5_out;  // AND_Gate and_1, 32 bits wide
  assign and_2_out = bit_extender_2_out & bit_extender_5_out;  // AND_Gate and_2, 32 bits wide
  assign and_3_out = bit_extender_3_out & bit_extender_6_out;  // AND_Gate and_3, 32 bits wide
  assign and_4_out = bit_extender_4_out & bit_extender_7_out;  // AND_Gate and_4, 32 bits wide
  assign out_2 = and_1_out | and_2_out | and_3_out | and_4_out;  // OR_Gate or_1, 32 bits wide

  // Notes on the sheet:
  //   lw
  //   imm
  //   sw
  //   beq
endmodule

module Register_File (
  input  [4:0] rs1,
  input  [4:0] rs2,
  input  [4:0] rd,
  input  [31:0] Write_Data,
  input  RegWEn,
  input  Clock,
  input  in_7,
  output [31:0] Read_Data_1,
  output [31:0] Read_Data_2
);

  wire and_1_out, and_2_out, and_3_out, and_4_out, and_5_out, and_6_out, and_7_out, and_8_out, and_9_out,
       n16x1_decoder_1_out0, n16x1_decoder_1_out1, n16x1_decoder_1_out2, n16x1_decoder_1_out5,
       n16x1_decoder_1_out6, n16x1_decoder_1_out7, n16x1_decoder_1_out8, n16x1_decoder_1_out9,
       n16x1_decoder_1_out10;
  wire [31:0] register_1_q, register_2_q, register_3_q, register_4_q, register_5_q, register_6_q,
       register_7_q, register_8_q, register_9_q;

  _16X1_Decoder u_16x1_decoder_1 (
    .in3(rd[3]), .in2(rd[2]), .in1(rd[1]), .in0(rd[0]), .out0(n16x1_decoder_1_out0),
    .out1(n16x1_decoder_1_out1), .out2(n16x1_decoder_1_out2), .out5(n16x1_decoder_1_out5),
    .out6(n16x1_decoder_1_out6), .out7(n16x1_decoder_1_out7), .out8(n16x1_decoder_1_out8),
    .out9(n16x1_decoder_1_out9), .out10(n16x1_decoder_1_out10));  // open: out3, out4, out11, out12, out13, out14, out15
  and and_1 (and_1_out, n16x1_decoder_1_out0, 1'b0);
  and and_2 (and_2_out, n16x1_decoder_1_out1, RegWEn);
  and and_3 (and_3_out, n16x1_decoder_1_out2, RegWEn);
  and and_4 (and_4_out, n16x1_decoder_1_out5, RegWEn);
  and and_5 (and_5_out, n16x1_decoder_1_out6, RegWEn);
  and and_6 (and_6_out, n16x1_decoder_1_out7, RegWEn);
  and and_7 (and_7_out, n16x1_decoder_1_out8, RegWEn);
  and and_8 (and_8_out, n16x1_decoder_1_out9, RegWEn);
  and and_9 (and_9_out, n16x1_decoder_1_out10, RegWEn);
  Register #(.width(32)) register_1 (.D(Write_Data), .en(and_1_out), .Q(register_1_q), .clk(Clock), .clr(in_7));
  Register #(.width(32)) register_2 (.D(Write_Data), .en(and_2_out), .Q(register_2_q), .clk(Clock), .clr(in_7));
  Register #(.width(32)) register_3 (.D(Write_Data), .en(and_3_out), .Q(register_3_q), .clk(Clock), .clr(in_7));
  Register #(.width(32)) register_4 (.D(Write_Data), .en(and_4_out), .Q(register_4_q), .clk(Clock), .clr(in_7));
  Register #(.width(32)) register_5 (.D(Write_Data), .en(and_5_out), .Q(register_5_q), .clk(Clock), .clr(in_7));
  Register #(.width(32)) register_6 (.D(Write_Data), .en(and_6_out), .Q(register_6_q), .clk(Clock), .clr(in_7));
  Register #(.width(32)) register_7 (.D(Write_Data), .en(and_7_out), .Q(register_7_q), .clk(Clock), .clr(in_7));
  Register #(.width(32)) register_8 (.D(Write_Data), .en(and_8_out), .Q(register_8_q), .clk(Clock), .clr(in_7));
  Register #(.width(32)) register_9 (.D(Write_Data), .en(and_9_out), .Q(register_9_q), .clk(Clock), .clr(in_7));
  _16X1_mux u_16x1_mux_1 (
    .in0(register_1_q), .in1(register_2_q), .in2(register_3_q), .in5(register_4_q), .in6(register_5_q),
    .sel3(rs1[3]), .sel2(rs1[2]), .sel1(rs1[1]), .in7(register_6_q), .sel0(rs1[0]), .in8(register_7_q),
    .in9(register_8_q), .in10(register_9_q), .\output (Read_Data_1));  // open: in3, in4, in11, in12, in13, in14, in15
  _16X1_mux u_16x1_mux_2 (
    .in0(register_1_q), .in1(register_2_q), .in2(register_3_q), .in5(register_4_q), .in6(register_5_q),
    .sel3(rs2[3]), .sel2(rs2[2]), .sel1(rs2[1]), .in7(register_6_q), .sel0(rs2[0]), .in8(register_7_q),
    .in9(register_8_q), .in10(register_9_q), .\output (Read_Data_2));  // open: in3, in4, in11, in12, in13, in14, in15
endmodule

module _4X1_Decoder (
  input  sel0,
  input  sel1,
  input  E,
  output out0,
  output out1,
  output out2,
  output out3
);

  wire not_1_out, not_2_out;

  not not_1 (not_1_out, sel0);
  not not_2 (not_2_out, sel1);
  and and_1 (out0, not_1_out, E, not_2_out);
  and and_2 (out1, sel0, E, not_2_out);
  and and_3 (out2, not_1_out, E, sel1);
  and and_4 (out3, sel0, E, sel1);
endmodule

module _16X1_Decoder (
  input  in3,
  input  in2,
  input  in1,
  input  in0,
  output out0,
  output out1,
  output out2,
  output out3,
  output out4,
  output out5,
  output out6,
  output out7,
  output out8,
  output out9,
  output out10,
  output out11,
  output out12,
  output out13,
  output out14,
  output out15
);

  wire n4x1_decoder_1_out0, n4x1_decoder_1_out1, n4x1_decoder_1_out2, n4x1_decoder_1_out3;

  _4X1_Decoder u_4x1_decoder_1 (
    .sel0(in2), .sel1(in3), .E(1'b1), .out0(n4x1_decoder_1_out0), .out1(n4x1_decoder_1_out1),
    .out2(n4x1_decoder_1_out2), .out3(n4x1_decoder_1_out3));
  _4X1_Decoder u_4x1_decoder_2 (
    .sel0(in0), .sel1(in1), .E(n4x1_decoder_1_out0), .out0(out0), .out1(out1), .out2(out2), .out3(out3));
  _4X1_Decoder u_4x1_decoder_3 (
    .sel0(in0), .sel1(in1), .E(n4x1_decoder_1_out1), .out0(out4), .out1(out5), .out2(out6), .out3(out7));
  _4X1_Decoder u_4x1_decoder_4 (
    .sel0(in0), .sel1(in1), .E(n4x1_decoder_1_out2), .out0(out8), .out1(out9), .out2(out10), .out3(out11));
  _4X1_Decoder u_4x1_decoder_5 (
    .sel0(in0), .sel1(in1), .E(n4x1_decoder_1_out3), .out0(out12), .out1(out13), .out2(out14), .out3(out15));
endmodule

module _2X1_mux_24_bit (
  input  [23:0] in_1,
  input  [23:0] in_2,
  input  in_3,
  output [23:0] out_4
);

  wire [23:0] and_1_out, and_2_out, bit_extender_1_out, not_1_out;

  assign bit_extender_1_out = {{23{in_3}}, in_3};  // Bit_Extender bit_extender_1
  assign not_1_out = ~bit_extender_1_out;  // NOT_Gate not_1, 24 bits wide
  assign and_1_out = in_1 & not_1_out;  // AND_Gate and_1, 24 bits wide
  assign and_2_out = in_2 & bit_extender_1_out;  // AND_Gate and_2, 24 bits wide
  assign out_4 = and_1_out | and_2_out;  // OR_Gate or_1, 24 bits wide
endmodule
